# Fritzing sketch gpio-fan (saved by Fritzing 0.9.2b)

parts:
  Raspberry_Pi = Raspberry Pi 3 [part_number=RPI-3-V1.2]
  F1 = Fan - Ventilador [package=THT]
  R1 = Resistor [tolerance=±5% resistance=4.7k package="2010 [SMD]"]
  Q1 = NPN-Transistor [part_number=BC337 package="TO92 [THT]"]

nets:
  N1: Raspberry_Pi.GND, Q1.E
  N2: Raspberry_Pi.GIPO21, R1.Pin_1
  5V: Raspberry_Pi.5V, F1.5V
  N3: F1.GND, Q1.C
  N4: R1.Pin_0, Q1.B

custom parts:
  Fan - Ventilador: Ventilador de 2 pines, se encuentra comunmente en computadoras de escritorio
