# Fritzing sketch gpio-fan_3.3v (saved by Fritzing 0.9.2b)

parts:
  Raspberry_Pi = Raspberry Pi 3 [part_number=RPI-3-V1.2]
  R1 = Resistor [tolerance=±5% resistance=4.7k package="2010 [SMD]"]
  Q1 = NPN-Transistor [part_number=BC337 package="TO92 [THT]"]
  3_3V = V_REG_LD1117VXX [package=78xxl]
  F1 = Fan - Ventilador [package=THT]

nets:
  GND: Raspberry_Pi.GND, Q1.E, 3_3V.GND
  N1: Raspberry_Pi.GIPO21, R1.Pin_1
  N2: Raspberry_Pi.5V, 3_3V.IN
  N3: R1.Pin_0, Q1.B
  N4: Q1.C, F1.GND
  N5: 3_3V.OUT, F1.5V

custom parts:
  Fan - Ventilador: Ventilador de 2 pines, se encuentra comunmente en computadoras de escritorio
