# Fritzing sketch gpio-fan_diode (saved by Fritzing 0.9.2b)

parts:
  Raspberry_Pi = Raspberry Pi 3 [part_number=RPI-3-V1.2]
  R1 = Resistor [tolerance=±5% resistance=4.7k package="2010 [SMD]"]
  Q1 = NPN-Transistor [part_number=BC337 package="TO92 [THT]"]
  Fan = Fan - Ventilador [package=THT]
  D2 = Diode [package=diode-hv]
  D1 = Diode [package=diode-hv]

nets:
  N1: Raspberry_Pi.GND, Q1.E
  N2: Raspberry_Pi.GIPO21, R1.Pin_1
  5V: Raspberry_Pi.5V, Fan.5V
  N3: R1.Pin_0, Q1.B
  N4: Q1.C, D2.C
  N5: Fan.GND, D1.A
  N6: D2.A, D1.C

custom parts:
  Fan - Ventilador: Ventilador de 2 pines, se encuentra comunmente en computadoras de escritorio
