# Fritzing sketch gpio-fan_transistor (saved by Fritzing 0.9.2b)

parts:
  Raspberry_Pi = Raspberry Pi 3 [part_number=RPI-3-V1.2]
  F1 = Fan - Ventilador [package=THT]
  R1 = Resistor [tolerance=±5% resistance=10k package="2010 [SMD]"]
  Q1 = NPN-Transistor [part_number=BC337 package="TO92 [THT]"]
  C1 = Capacitor Polarized [part_number=10µF package=panasonic_c]
  R2 = Resistor [tolerance=±5% resistance=330 package="2010 [SMD]"]

nets:
  N1: Raspberry_Pi.GND, Q1.E
  5V: Raspberry_Pi.5V, F1.5V
  N2: F1.GND, Q1.C
  N3: R1.Pin_0, Q1.B, C1.-
  N4: R1.Pin_1, C1.+, R2.Pin_0

custom parts:
  Fan - Ventilador: Ventilador de 2 pines, se encuentra comunmente en computadoras de escritorio
